# Fritzing sketch scheme (saved by Fritzing 0.9.3b)

parts:
  Raspberry_Pi_1 = Raspberry Pi 3 [part_number=RPI-3-V1.2]  # not connected
  J1 = Piezo Speaker  # not connected
  U1 = RFID RC522 SIP - 8 pins [chip_label="RFID RC522" package="SIP (Single Inline) [THT]"]  # not connected
  Composant1 = HC-SR501 Body Sensor Module  # not connected
  RGB_Strip_LED1 = RGB Strip LED  # not connected
  Q4 = TIP120 Hi-Current Darlington Transistor  # not connected
  Q5 = TIP120 Hi-Current Darlington Transistor  # not connected
  Q6 = TIP120 Hi-Current Darlington Transistor  # not connected
  JACK1 = 2.1mm Barrel Jack with Terminal Block
  J2 = screw terminal, 10 pins
  J3 = screw terminal, 10 pins

nets:
  N1: JACK1.POS, J3.pin10
  N2: JACK1.NEG, J2.pin1

notes:
  To screen
  Buzzer
  Raspberry
  RFID reader
  PIR Sensor
  LED strip
  Transistors

custom parts:
  RFID RC522 SIP - 8 pins: A SIP stand-in part for RFID RC522 . With 8 pins on a 300 mil single inline package (SIP) footprint.
  HC-SR501 Body Sensor Module: Pyroelectric Infrared PIR Motion Sensor Detector Module
  RGB Strip LED: A tri-color Strip LED with red, green and blue. Based on LED SMD 5050 RGB Pin order: common cathode - green - red - blue
